# Fritzing sketch Bartosz.Nowakowski (saved by Fritzing 0.9.3b)
circuit board: 2.92807cm x 5.04901cm
breadboards: 1

parts:
  WeMos_D1_Mini1 = WeMos D1 Mini
  R1 = Resistor [tolerance=±5% resistance=220 package=THT]
  Water_Level_Sensor1 = Water Level Sensor

nets:
  3V3: WeMos_D1_Mini1.3V3, Water_Level_Sensor1.VCC
  N1: WeMos_D1_Mini1.A0, R1.Pin_0
  N2: WeMos_D1_Mini1.G, Water_Level_Sensor1.GND
  N3: R1.Pin_1, Water_Level_Sensor1.SIG

custom parts:
  Water Level Sensor: A water level sensor. This sensor operates at 3V to 5V. The Sig (signal) pin outputs an analogue signal that is in proportion to the amount of water in contact with the sensor.
